// Logisim project cpu.circ as structural Verilog: 4 circuits, main circuit cpu
module cpu (
  input  clk,
  input  ram_end,
  input  [31:0] ram_data,
  output [31:0] ram_read_addr,
  output cpu_end
);

  wire and_1_out, and_3_out, data_path_1_p11, data_path_1_p12, data_path_1_p16, \end , eq, greater, halt,
       immediate, inm_comp_q, is_comparission, less, not_1_out, not_2_out, not_3_out, or_2_out, rw, rw_0,
       rw_1;
  wire [1:0] data_selector;
  wire [3:0] alu_selector;
  wire [4:0] DA, register_d, register_s, register_t;
  wire [5:0] func_code, op_code;
  wire [25:0] jump;
  wire [31:0] \const , constant, multiplexer_2_out, multiplexer_3_out, multiplexer_4_out, pc_next, ram;

  not not_1 (not_1_out, halt);
  not not_2 (not_2_out, halt);
  and and_1 (and_1_out, immediate, not_2_out, is_comparission);
  Register #(.width(32)) PC (.D(pc_next), .en(\end ), .Q(ram_read_addr), .clk(clk));  // open: clr
  and and_2 (\end , ram_end, not_1_out);
  Multiplexer #(.width(5)) multiplexer_1 (.in0(register_d), .in1(register_t), .out(DA), .sel(immediate));  // open: en
  D_Flip_Flop #(.trigger("high")) inm_comp (.clk(clk), .D(and_1_out), .Q(inm_comp_q));  // open: Qn, preset, en, reset
  branch_control branch_control_1 (
    .PC_in(ram_read_addr), .jump(1'b0), .flag(1'b0), .offset({16{1'b0}}), .PC_out(pc_next));
  D_Flip_Flop d_ff_1 (.clk(clk), .D(\end ), .Q(cpu_end));  // open: Qn, preset, en, reset
  D_Flip_Flop #(.trigger("high")) inm_comp_2 (.clk(clk), .D(inm_comp_q), .Q(rw_1));  // open: Qn, preset, en, reset
  or or_1 (rw, rw_0, rw_1);
  // instruction_decoder instruction_decoder_1: pin names not known; wires that end beside it: ram_data, op_code, register_s, register_t, register_d, func_code, \const , jump, alu_selector, immediate, data_selector, rw_0, halt, is_comparission
  Multiplexer #(.width(32)) multiplexer_2 (
    .in0({32{1'b0}}), .in1(32'h1), .out(multiplexer_2_out), .sel(eq));  // open: en
  Multiplexer #(.width(32)) multiplexer_3 (
    .in0({32{1'b0}}), .in1(32'h1), .out(multiplexer_3_out), .sel(greater));  // open: en
  Multiplexer #(.width(32)) multiplexer_4 (
    .in0(multiplexer_2_out), .in1(multiplexer_3_out), .out(multiplexer_4_out), .sel(immediate));  // open: en
  and and_3 (and_3_out, is_comparission, or_2_out);
  // data_path data_path_1: pin names not known; wires that end beside it: register_s, register_t, DA, rw, constant, ram, \end , alu_selector, data_selector, immediate, data_path_1_p11, data_path_1_p12, greater, eq, less, data_path_1_p16
  Multiplexer #(.width(32)) multiplexer_5 (
    .in0(\const ), .in1(multiplexer_4_out), .out(constant), .sel(and_3_out));  // open: en
  or or_2 (or_2_out, rw_1, not_3_out);
  not not_3 (not_3_out, immediate);

  // Other names for the same wires on the sheet: instruction[31:0] = ram_data; pc_current[31:0] = ram_read_addr;
  //   wait = rw_1
endmodule

module cpu_test (
);

  wire clock_1_out, \end , fake_ram_1_end;
  wire [31:0] addr, fake_ram_1_data;

  fake_ram fake_ram_1 (
    .cycles(4'b0011), .clk(clock_1_out), .db0(32'h1), .db1(32'h2), .db2(32'h3), .db3(32'h4), .ad(addr),
    .data(fake_ram_1_data), .\end (fake_ram_1_end), .cpu_end(\end ));  // open: real_addr
  // Probe on fake_ram_1_data
  Clock clock_1 (.out(clock_1_out));
  cpu cpu_1 (
    .ram_end(fake_ram_1_end), .ram_data(fake_ram_1_data), .ram_read_addr(addr), .clk(clock_1_out),
    .cpu_end(\end ));
  // Probe on addr
endmodule

module fake_ram (
  input  [3:0] cycles,
  input  clk,
  input  [31:0] db0,
  input  cpu_end,
  input  [31:0] db1,
  input  [31:0] db2,
  input  [31:0] db3,
  input  [31:0] ad,
  output [31:0] data,
  output \end ,
  output [15:0] real_addr
);

  wire [1:0] db_flag;
  wire [31:0] blocks;
  wire [31:2] divider_2_out;
  wire [31:16] arddr;

  Divider #(.width(32)) divider_1 (.a(ad), .b(32'h10), .out({arddr, real_addr}), .rem(blocks));  // open: upper
  Multiplexer #(.select(2), .width(32), .enable("false")) multiplexer_1 (
    .in0(db0), .in1(db1), .in2(db2), .in3(db3), .out(data), .sel(db_flag));
  Divider #(.width(32)) divider_2 (.a(blocks), .b(32'h4), .out({divider_2_out, db_flag}));  // open: upper, rem
  waita waita_1 (.cycles(cycles), .clk(clk), .cpu_end(cpu_end), .\end (\end ));

  // Other names for the same wires on the sheet: arddr[15:0] = real_addr; real_arddr[15:0] = real_addr
endmodule

module waita (
  input  clk,
  input  [3:0] cycles,
  input  cpu_end,
  output \end 
);

  wire not_1_out;
  wire [3:0] counter_1_q;

  Counter #(.width(4), .max('hf)) counter_1 (
    .count(not_1_out), .Q(counter_1_q), .clk(clk), .clr(cpu_end));  // open: load, D, carry
  not not_1 (not_1_out, \end );
  Comparator #(.width(4)) comparator_1 (.a(counter_1_q), .b(cycles), .eq(\end ));  // open: gt, lt
endmodule
